# Fritzing sketch imx6ul_schematics (saved by Fritzing 0.9.3b)
breadboards: 1

parts:
  Squix1 = OLED 0.96" 128x64 I2C SSD1306
  PICO-PI-IMX6UL = Raspberry Pi 3 [part_number=RPI-3-V1.2]
  BUTTON_PLAY_PAUSE = Pushbutton [package="[THT]"]
  BUTTON_VOLUME_UP = Pushbutton [package="[THT]"]
  BUTTON_VOLUME_DOWN = Pushbutton [package="[THT]"]
  BUTTON_PRESET1 = Pushbutton [package="[THT]"]
  BUTTON_PRESET2 = Pushbutton [package="[THT]"]
  R1 = Resistor [tolerance=±5% resistance=1k package=THT]
  R2 = Resistor [tolerance=±5% resistance=1k package=THT]
  R3 = Resistor [tolerance=±5% resistance=1k package=THT]
  R4 = Resistor [tolerance=±5% resistance=1k package=THT]
  R5 = Resistor [tolerance=±5% resistance=1k package=THT]

nets:
  VCC: Squix1.VCC, PICO-PI-IMX6UL.5V
  GND: Squix1.GND, PICO-PI-IMX6UL.GND, R1.Pin_0, R2.Pin_0, R3.Pin_0, R4.Pin_0, R5.Pin_0
  N1: Squix1.SCL, PICO-PI-IMX6UL.GPIO3
  N2: Squix1.SCA, PICO-PI-IMX6UL.GPIO2
  N3: PICO-PI-IMX6UL.3v3, BUTTON_PLAY_PAUSE.Pin_1, BUTTON_PLAY_PAUSE.Pin_2, BUTTON_VOLUME_UP.Pin_1, BUTTON_VOLUME_UP.Pin_2, BUTTON_VOLUME_DOWN.Pin_1, BUTTON_VOLUME_DOWN.Pin_2, BUTTON_PRESET1.Pin_1, BUTTON_PRESET1.Pin_2, BUTTON_PRESET2.Pin_1, BUTTON_PRESET2.Pin_2
  N4: PICO-PI-IMX6UL.GIPO5, BUTTON_VOLUME_DOWN.Pin_3, BUTTON_VOLUME_DOWN.Pin_4, R3.Pin_1
  N5: PICO-PI-IMX6UL.GIPO6, BUTTON_PRESET1.Pin_3, BUTTON_PRESET1.Pin_4, R4.Pin_1
  N6: PICO-PI-IMX6UL.GIPO13, BUTTON_PRESET2.Pin_3, BUTTON_PRESET2.Pin_4, R5.Pin_1
  N7: PICO-PI-IMX6UL.GIPO19, BUTTON_VOLUME_UP.Pin_3, BUTTON_VOLUME_UP.Pin_4, R2.Pin_1
  N8: PICO-PI-IMX6UL.GIPO16, BUTTON_PLAY_PAUSE.Pin_3, BUTTON_PLAY_PAUSE.Pin_4, R1.Pin_1

notes:
  1st row = 3.3V rail
  2nd row = GND rail
  1kOhm Pull-Down resistors to guarantee a stable default state.
  PLAY_PAUSE VOLUME_UP VOLUME_DOWN PRESET1 PRESET2
  GPIO5_IO02 GPIO4_IO19 GPIO4_IO21 GPIO4_IO22 GPIO4_IO23
